# Fritzing sketch ksp-gegi-breadboard (saved by Fritzing 0.9.2b)
breadboards: 1

parts:
  Part4 = Arduino Pro Mini v13
  Pro_Micro1 = Pro Micro
  SHIFT1 = TPIC6B595
  Joystick1 = Thumb Joystick
  Joystick2 = Thumb Joystick
  STAGEMODE = Toggle Switch [package=THT]
  STAGE = Round Pushbutton
  LEDYlowfuel = LED - 5mm [color="Yellow (595nm)" package="5 mm [THT]"]
  R1 = Resistor [tolerance=±5% resistance=220 package=THT]
  R2 = Resistor [tolerance=±5% resistance=220 package=THT]
  LEDR0 = LED - 5mm [color="Red (633nm)" package="5 mm [THT]"]
  LEDG0 = LED - 5mm [color="Green (560nm)" package="5 mm [THT]"]
  R3 = Resistor [tolerance=±5% resistance=220 package=THT]
  LCM1602_IIC1 = LCM1602 IIC [part_number="LCM1602 IIC" chip_label="LCM1602 IIC" package="DIP (Dual Inline) [THT]"]
  U1 = LCD-16X2 [package=lcd-16x2]
  Squix1 = OLED 0.96" 128x64 I2C SSD1306  # not connected

nets:
  GND: Part4.GND, Pro_Micro1.GND, SHIFT1.GND, Joystick1.GND, Joystick2.GND, STAGEMODE.L2, STAGE.leg1, R1.Pin_1, LCM1602_IIC1.GND
  VCC: Part4.VCC, Pro_Micro1.VCC, Joystick1.VCC, Joystick2.VCC, LEDR0.anode, LEDG0.anode, LCM1602_IIC1.VCC
  N1: Part4.D12/MISO, LEDYlowfuel.anode
  N2: Part4.D11_PWM/MOSI, STAGEMODE.COM
  N3: Part4.D10_PWM/SS, STAGE.leg0
  N4: Part4.D1/RX, Pro_Micro1.TX1
  N5: Part4.D0/TX, Pro_Micro1.RX0
  N6: Pro_Micro1.D2, LCM1602_IIC1.SDA
  N7: Pro_Micro1.D3, LCM1602_IIC1.SCL
  N8: Pro_Micro1.D5, Joystick1.SEL
  N9: Pro_Micro1.D7, Joystick2.SEL
  N10: Pro_Micro1.D18/A0, Joystick1.HORZ
  N11: Pro_Micro1.D19/A1, Joystick1.VERT
  N12: Pro_Micro1.D20/A2, Joystick2.HORZ
  N13: Pro_Micro1.D21/A3, Joystick2.VERT
  N14: SHIFT1.DRAIN0, R3.Pin_0
  N15: SHIFT1.DRAIN4, R2.Pin_1
  N16: LEDYlowfuel.cathode, R1.Pin_0
  N17: R2.Pin_0, LEDR0.cathode
  N18: LEDG0.cathode, R3.Pin_1
  VSS: LCM1602_IIC1.VSS, U1.VSS
  VDD: LCM1602_IIC1.VDD, U1.VDD
  N19: LCM1602_IIC1.V0, U1.VO
  N20: LCM1602_IIC1.RS, U1.RS
  N21: LCM1602_IIC1.RW, U1.R_W
  N22: LCM1602_IIC1.E, U1.E
  N23: LCM1602_IIC1.D0, U1.DB0
  N24: LCM1602_IIC1.D1, U1.DB1
  N25: LCM1602_IIC1.D2, U1.DB2
  N26: LCM1602_IIC1.D3, U1.DB3
  N27: LCM1602_IIC1.D4, U1.DB4
  N28: LCM1602_IIC1.D5, U1.DB5
  N29: LCM1602_IIC1.D6, U1.DB6
  N30: LCM1602_IIC1.D7, U1.DB7
  N31: LCM1602_IIC1.A, U1.A
  N32: LCM1602_IIC1.K, U1.K
  N33: LCM1602_IIC1.LED_A, LCM1602_IIC1.LED_B

notes:
  Drain0-3 = GREEN
  (lights/gear/rcs/sas) through resistor to VCC
  Drain4-7 = RED
  (lights/gear/rcs/sas) through resistor to VCC
  LEDY1/2, LEDoverheat
  (12/13/14) through resistor to GND
  SWITCHES to GND
  2+3 (2toggle), 4+5 (2toggle), 6/7/8/9 (toggle), 10 (push), 11 (toggle)
  LCD 16x2, OLED 128x64 on I2C BUS from 2(SDA)+3(SCL) from MICRO
  Analog Voltmeters on pins PWM 9, 10 to GND from MICRO
  Potentiometers throttle/timewarp on pins 4, 8 from MICRO

custom parts:
  Pro Micro: The SparkFun Pro Micro is a complete USB-based microcontoller development system, in a very small footprint, capable of implementing many types of projects. All programming can be done via the USB port.
  TPIC6B595: 8-bit high-power parallel-load shift register
  LCM1602 IIC: I2C-Module to use a 1602 or 2004 LCD on with the wire.h libory Serial LCD Modul
