# Fritzing sketch ksp-gegi-perfboard (saved by Fritzing 0.9.2b)
perfboards: 1

parts:
  Pro_Micro2 = Pro Micro
  SHIFT1 = TPIC6B595
  Part4 = Arduino Pro Mini v13

nets:
  VCC: Pro_Micro2.VCC, SHIFT1.SRCLR, SHIFT1.VCC, Part4.VCC
  N1: Pro_Micro2.GND, SHIFT1.GND#18
  N2: SHIFT1.SER_IN, Part4.A2
  N3: SHIFT1.G, SHIFT1.GND#9
  N4: SHIFT1.GND#10, Part4.GND
  N5: SHIFT1.RCK, Part4.A3
  N6: SHIFT1.SRCK, Part4.A1

custom parts:
  Pro Micro: The SparkFun Pro Micro is a complete USB-based microcontoller development system, in a very small footprint, capable of implementing many types of projects. All programming can be done via the USB port.
  TPIC6B595: 8-bit high-power parallel-load shift register
